# Fritzing sketch Accelerometer_ADXL337 (saved by Fritzing 0.9.3b)

parts:
  Part1 = Bela
  Part2 = Triple Axis Accelerometer Breakout - ADXL335

nets:
  N1: Part1.P9_01_GND, Part2.GND
  N2: Part1.P9_03_3.3V, Part2.VCC
  N3: Part1.Ain_00, Part2.XOUT
  N4: Part1.Ain_01, Part2.YOUT
  N5: Part1.Ain_02, Part2.ZOUT

custom parts:
  Bela: Bela low-latency audio/sensor platform
