# Fritzing sketch DIPswitchSPST (saved by Fritzing 0.9.3b)
breadboards: 1

parts:
  Part1 = Bela
  SW1 = DIP SWITCH [package=dipswitch-02]
  SW2 = DIP SWITCH [package=dipswitch-02]
  R1 = Resistor [tolerance=±5% resistance=10k package=THT]
  R2 = Resistor [tolerance=±5% resistance=10k package=THT]
  R3 = Resistor [tolerance=±5% resistance=10k package=THT]
  R4 = Resistor [tolerance=±5% resistance=10k package=THT]

nets:
  N1: Part1.D_00, SW1.2, R1.Pin_1
  N2: Part1.D_01, SW1.1, R2.Pin_1
  N3: Part1.D_02, SW2.2, R3.Pin_1
  N4: Part1.D_03, SW2.1, R4.Pin_1
  N5: Part1.P9_01_GND, R2.Pin_0, R3.Pin_0, R4.Pin_0
  N6: Part1.P9_03_3.3V, SW1.3

notes:
  The resistors are 10k Ohm.
  Connect only as many switches as needed.

custom parts:
  Bela: Bela low-latency audio/sensor platform
