# Fritzing sketch ElectrectMicrophone (saved by Fritzing 0.9.3b)
breadboards: 1

parts:
  Part3 = Bela
  Part4 = Bela
  SparkFun_Electret_Microphone_Breakout4 = SparkFun Electret Microphone Breakout [part_number=BOB-09964]
  SparkFun_Electret_Microphone_Breakout5 = SparkFun Electret Microphone Breakout [part_number=BOB-09964]
  R7 = Resistor [tolerance=±5% resistance=1M package=THT]
  R8 = Resistor [tolerance=±5% resistance=1M package=THT]

nets:
  N1: Part3.P9_01_GND, SparkFun_Electret_Microphone_Breakout4.GND, R8.Pin_1
  N2: Part3.P9_03_3.3V, SparkFun_Electret_Microphone_Breakout4.VCC, R7.Pin_0
  N3: Part3.Ain_00, SparkFun_Electret_Microphone_Breakout4.AUD, R7.Pin_1, R8.Pin_0
  N4: Part4.P9_01_GND, SparkFun_Electret_Microphone_Breakout5.GND
  N5: Part4.P9_03_3.3V, SparkFun_Electret_Microphone_Breakout5.VCC
  N6: Part4.Aout_01, Part4.In_L, SparkFun_Electret_Microphone_Breakout5.AUD

notes:
  Connected to bipolar audio ADC
  Connected to unipolar non-audio ADC
  The resistors are 1M Ohm

custom parts:
  Bela: Bela low-latency audio/sensor platform
  SparkFun Electret Microphone Breakout: Ready to add audio to your next project? This small breakout board couples a small electret microphone with a 100x opamp to amplify the sounds of voice, door knocks, etc loud enough to be picked up by a microcontroller’s Analog to Digital converter. Unit comes fully assembled as shown. Works from 2.7V up to 5.5V.
