# Fritzing sketch Flex (saved by Fritzing 0.9.3b)
breadboards: 1

parts:
  Part1 = Bela
  R5 = Resistor [tolerance=±5% resistance=47k package="2010 [SMD]"]
  R6 = Basic Flex Resistor

nets:
  N1: Part1.P9_01_GND, R5.Pin_1
  N2: Part1.P9_03_3.3V, R6.Pin_2
  N3: Part1.Ain_00, R5.Pin_0, R6.pin_1

notes:
  The resistor is 47k Ohm.

custom parts:
  Bela: Bela low-latency audio/sensor platform
