# Fritzing sketch ForceSensitiveResistor (saved by Fritzing 0.9.3b)
breadboards: 1

parts:
  Part1 = Bela
  J1 = Basic Force Sensing Resistor (FSR) [package=THT]
  R1 = Resistor [tolerance=±5% resistance=3.3k package="2010 [SMD]"]

nets:
  N1: Part1.P9_01_GND, R1.Pin_1
  N2: Part1.P9_03_3.3V, J1.pin_1
  N3: Part1.Ain_00, J1.pin_0, R1.Pin_0

notes:
  The resistor is 3.3k Ohm.

custom parts:
  Bela: Bela low-latency audio/sensor platform
