# Fritzing sketch InertialMeasurementUnit_LSM9DS1 (saved by Fritzing 0.9.3b)

parts:
  Part1 = Bela
  LSM9DS1 = SparkFun-LSM9DS1-Breakout [part_number=SEN-13284]

nets:
  N1: Part1.P9_01_GND, LSM9DS1.GND
  N2: Part1.P9_03_3.3V, LSM9DS1.VDD

custom parts:
  Bela: Bela low-latency audio/sensor platform
  SparkFun-LSM9DS1-Breakout: The LSM9DS1 is a versatile, motion-sensing system-in-a-chip. It houses a 3-axis accelerometer, 3-axis gyroscope, and 3-axis magnetometer – nine degrees of freedom (9DOF) in a single IC! The LSM9DS1 is equipped with a digital interface, but even that is flexible: it supports both I2C and SPI, so you’ll be hard-pressed to find a microcontroller it doesn’t work with. Each sensor in the LSM9DS1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
