# Fritzing sketch InfraredDistance_GP2Y0A21YK0F (saved by Fritzing 0.9.3b)

parts:
  Part1 = Bela
  J1 = Infrared Proximity Sensor

nets:
  N1: Part1.P9_01_GND, J1.GND
  N2: Part1.Ain_00, J1.Vout
  N3: Part1.Aout_5V, J1.Vcc

notes:
  Be Careful
  This sensor is powered by 5V!

custom parts:
  Bela: Bela low-latency audio/sensor platform
