# Fritzing sketch LightDependantResistor (saved by Fritzing 0.9.3b)
breadboards: 1

parts:
  Part1 = Bela
  R4 = Photocell (LDR) [package=THT]
  R5 = Resistor [tolerance=±5% resistance=4.7k package="2010 [SMD]"]

nets:
  N1: Part1.P9_01_GND, R5.Pin_1
  N2: Part1.P9_03_3.3V, R4.pin_1
  N3: Part1.Ain_00, R4.pin_0, R5.Pin_0

notes:
  The resistor is 4.7k Ohm.

custom parts:
  Bela: Bela low-latency audio/sensor platform
