# Fritzing sketch MomentaryButtonSPST&RotaryPotentiometer (saved by Fritzing 0.9.3b)
breadboards: 1

parts:
  Part1 = Bela
  S1 = Pushbutton [package="[SMD]"]
  R1 = Resistor [tolerance=±5% resistance=10k package=THT]
  R2 = Rotary Potentiometer (Small) [maximum_resistance=10kΩ package=THT]

nets:
  N1: Part1.D_00, S1.Pin_3, S1.Pin_4, R1.Pin_1
  N2: Part1.P9_01_GND, R1.Pin_0, R2.leg2
  N3: Part1.P9_03_3.3V, R2.leg1
  N4: Part1.Ain_00, R2.wiper
  N5: S1.Pin_1, S1.Pin_2

custom parts:
  Bela: Bela low-latency audio/sensor platform
