# Fritzing sketch MomentaryButtonSPST (saved by Fritzing 0.9.3b)
breadboards: 1

parts:
  Part1 = Bela
  S1 = Pushbutton [package="[SMD]"]
  R1 = Resistor [tolerance=±5% resistance=10k package=THT]

nets:
  N1: Part1.D_00, S1.Pin_3, S1.Pin_4, R1.Pin_1
  N2: Part1.P9_01_GND, R1.Pin_0
  N3: S1.Pin_1, S1.Pin_2

custom parts:
  Bela: Bela low-latency audio/sensor platform
