# Fritzing sketch PassiveSpeaker (saved by Fritzing 0.9.3b)

parts:
  Part1 = Bela
  SP1 = SPEAKER [package=pcb_mount_speaker]
  SP2 = SPEAKER [package=pcb_mount_speaker]

nets:
  N1: Part1.Spkr_R+, SP1.-
  N2: Part1.Spkr_R-, SP1.+
  N3: Part1.Spkr_L+, SP2.-
  N4: Part1.Spkr_L-, SP2.+

custom parts:
  Bela: Bela low-latency audio/sensor platform
