# Fritzing sketch PiezoElement (saved by Fritzing 0.9.3b)
breadboards: 2

parts:
  Part1 = Bela
  J1 = Piezo Speaker
  R5 = Resistor [tolerance=±5% resistance=1M package=THT]
  R6 = Resistor [tolerance=±5% resistance=1M package=THT]
  Part2 = Bela
  J2 = Piezo Speaker
  R7 = Resistor [tolerance=±5% resistance=220 package=THT]

nets:
  N1: Part1.P9_01_GND, J1.pin1, R5.Pin_1
  N2: Part1.P9_03_3.3V, R6.Pin_0
  N3: Part1.Ain_00, J1.pin2, R5.Pin_0, R6.Pin_1
  N4: Part2.P9_01_GND, J2.pin1
  N5: Part2.P9_03_3.3V, R7.Pin_0
  N6: Part2.In_L, J2.pin2, R7.Pin_1

notes:
  Connected to unipolar non-audio ADC
  Resistors are 1M Ohm.
  Connected to bipolar audio ADC
  Resistor is 220 Ohm.

custom parts:
  Bela: Bela low-latency audio/sensor platform
