# Fritzing sketch RGBcommonCathodeLED (saved by Fritzing 0.9.3b)
breadboards: 1

parts:
  Part1 = Bela
  R2 = Resistor [tolerance=±5% resistance=220 package=THT]
  R3 = Resistor [tolerance=±5% resistance=220 package=THT]
  R4 = Resistor [tolerance=±5% resistance=220 package=THT]
  LED3 = RGB LED (com. cathode, rgb) [package="5 mm [THT]"]

nets:
  N1: Part1.D_00, R2.Pin_1
  N2: Part1.D_01, R4.Pin_1
  N3: Part1.D_02, R3.Pin_1
  N4: R4.Pin_0, LED3.green_anode

notes:
  The Cathode (-) is the longest pin, connected to GND.
  To control the brightness of the LED, drive it with a PWM signal with friequency of 50 Hz. The duty cycle of the PWM signal determines the LED brightness.
  To generate the PWM signal driving the LED, use either an analog output (preferred, if available) or a digital output configured to work at audio rate.
  Resistors are 220 Ohm.

custom parts:
  Bela: Bela low-latency audio/sensor platform
