# Fritzing sketch RotaryPotentiometer (saved by Fritzing 0.9.3b)
breadboards: 1

parts:
  Part1 = Bela
  R1 = Rotary Potentiometer (Small) [maximum_resistance=100kΩ package=THT]

nets:
  N1: Part1.P9_01_GND, R1.leg2
  N2: Part1.P9_03_3.3V, R1.leg1
  N3: Part1.Ain_00, R1.wiper

custom parts:
  Bela: Bela low-latency audio/sensor platform
