# Fritzing sketch SingleColorLED (saved by Fritzing 0.9.3b)
breadboards: 1

parts:
  Part1 = Bela
  LED2 = smd LED [color="Red (633nm)" package="1206 [SMD]"]
  R1 = Resistor [tolerance=±5% resistance=220 package=THT]

nets:
  N1: Part1.D_00, LED2.anode
  N2: Part1.P9_01_GND, R1.Pin_1
  N3: LED2.cathode, R1.Pin_0

notes:
  The Anode (+) is the longest pin, connected to the Bela output.
  To control the brightness of the LED, drive it with a PWM signal with friequency of 50 Hz. The duty cycle of the PWM signal determines the LED brightness.
  To generate the PWM signal driving the LED, use either an analog output (preferred, if available) or a digital output configured to work at audio rate.
  Resistor is 220 Ohm.

custom parts:
  Bela: Bela low-latency audio/sensor platform
