# Fritzing sketch SoftMembranePotentiometer (saved by Fritzing 0.9.3b)
breadboards: 1

parts:
  Part1 = Bela
  SparkFun1 = SoftPot Membrane Potentiometer - 50mm [part_number=SEN-08680]

nets:
  N1: Part1.P9_01_GND, SparkFun1.leg1
  N2: Part1.P9_03_3.3V, SparkFun1.leg2
  N3: Part1.Ain_00, SparkFun1.wiper

custom parts:
  Bela: Bela low-latency audio/sensor platform
  SoftPot Membrane Potentiometer - 50mm: These are very thin variable potentiometers. By pressing down on various parts of the strip, the resistance linearly changes from 100Ohms to 10,000Ohms allowing the user to very accurately calculate the relative position on the strip. Can be used as an accurate positional indicator for CNC head positioning, variable user input (volume level input for example), straight user input (multiple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
