# Fritzing sketch SwitchSPDT (saved by Fritzing 0.9.3b)
breadboards: 1

parts:
  Part1 = Bela
  U1 = SWITCH_SPDT [package=kps-1290]

nets:
  N1: Part1.D_00, U1.P
  N2: Part1.P9_01_GND, U1.S
  N3: Part1.P9_03_3.3V, U1.O

custom parts:
  Bela: Bela low-latency audio/sensor platform
