# Fritzing sketch ThumbJoystickwithButton (saved by Fritzing 0.9.3b)
breadboards: 1

parts:
  Part1 = Bela
  R1 = Resistor [tolerance=±5% resistance=10k package=THT]
  Part5 = Adafruit Analog 2-Axis Joystick [part_number="Adafruit #512"]

nets:
  N1: Part1.D_00, R1.Pin_1, Part5.SWITCH
  N2: Part1.P9_01_GND, Part5.GND
  N3: Part1.P9_03_3.3V, R1.Pin_0, Part5.VCC
  N4: Part1.Ain_00, Part5.XOUT
  N5: Part1.Ain_01, Part5.YOUT

notes:
  The resistor is 10k Ohm.
  Connect the switch only if needed.

custom parts:
  Bela: Bela low-latency audio/sensor platform
  Adafruit Analog 2-Axis Joystick: This mini-kit makes it easy to mount a PSP/Xbox-like thumb joystick to your project. The thumbstick is an analog joystick - more accurate and sensitive than just 'directional' joysticks - with a 'press in to select' button. Since it's analog, you'll need two analog reading pins on your microcontroller to determine X and Y. Having an extra digital input will let you read the switch. The pack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
