# Fritzing sketch TrillCraft (saved by Fritzing 0.9.3b)

parts:
  Part1 = Bela
  Trill_Craft1 = Trill Craft

nets:
  N1: Part1.P9_01_GND, Trill_Craft1.GND
  N2: Part1.P9_03_3.3V, Trill_Craft1.VCC

custom parts:
  Bela: Bela low-latency audio/sensor platform
  Trill Craft: A 30-channel breakout board for building touch interfaces out of any conductive material, by Bela.io
