# Fritzing sketch UltrasoundDistance_HCSR04 (saved by Fritzing 0.9.3b)
breadboards: 1

parts:
  Part1 = Bela
  HC-SR04_Sensor_1 = HC-SR04 Ultrasonic Distance Sensor
  R1 = Resistor [tolerance=±5% resistance=2.2k package=THT]
  R2 = Resistor [tolerance=±5% resistance=3.3k package=THT]

nets:
  N1: Part1.D_01, R1.Pin_1, R2.Pin_0
  N2: Part1.P9_01_GND, HC-SR04_Sensor_1.GND, R2.Pin_1
  N3: Part1.Aout_00, HC-SR04_Sensor_1.TRIG
  N4: Part1.Aout_5V, HC-SR04_Sensor_1.VCC
  N5: HC-SR04_Sensor_1.ECHO, R1.Pin_0

notes:
  Be Careful !
  This circuit is powered by 5V.
  Resistors are 2.2k Ohm (top) and 3.3k Ohm (bottom).

custom parts:
  Bela: Bela low-latency audio/sensor platform
