# Fritzing sketch VibrationMotor (saved by Fritzing 0.9.3b)
breadboards: 1

parts:
  Part1 = Bela
  MOTOR1 = Vibration Motor
  D1 = Rectifier Diode [part_number=1N4001 package="300 mil [THT]"]
  C2 = Ceramic Capacitor [capacitance=0.1µF package="200 mil [THT, multilayer]"]
  R1 = Resistor [tolerance=±5% resistance=1k package="2010 [SMD]"]
  Q1 = NPN-Transistor [package="SOT-23 [SMD]"]

nets:
  N1: Part1.D_00, R1.Pin_1
  N2: Part1.P9_01_GND, Q1.2
  N3: Part1.Aout_5V, MOTOR1.POS, D1.cathode, C2.1
  N4: MOTOR1.NEG, D1.anode, C2.0, Q1.1
  N5: R1.Pin_0, Q1.0

notes:
  Be Careful !
  This circuit is powered by 5V.
  The circuit should work also is powered with 3.3V, but the intensity of the vibration may be weaker.
  To control the vibration intensity of the motor, drive it with a PWM signal with friequency of 50 to 100 Hz. The duty cycle of the PWM signal determines the vibration intensity.
  To generate the PWM signal driving the motor, use either an analog output (preferred, if available) or a digital output configured to work at audio rate.
  The resistor is 1k Ohm.
  The transistor is a generic NPN (such as the 2N3904). The top pin is the Collector (C), the middle pin is the Base (B), and the bottom pin the Emitter (E).
  The diode is 1N4001.
  The capacitor is ceramic 0.1uF.
  C
  E
  B

custom parts:
  Bela: Bela low-latency audio/sensor platform
  Vibration Motor: An eccentric vibration motor!
