# Fritzing sketch MCT4054_W2-2 (saved by Fritzing 0.9.3b)
breadboards: 1

parts:
  Part1 = Bela
  R2 = Slide Potentiometer [maximum_resistance=100kΩ]  # not connected
  R3 = Rotary Potentiometer (Small) [maximum_resistance=100kΩ package=THT]
  R4 = Resistor [tolerance=±5% resistance=10k package="0402 [SMD]"]
  R5 = Resistor [tolerance=±5% resistance=10k package="0402 [SMD]"]

nets:
  N1: Part1.P9_01_GND, R5.Pin_1
  N2: Part1.P9_03_3.3V, R3.leg2, R4.Pin_0
  N3: Part1.Ain_01, R3.wiper
  N4: R3.leg1, R4.Pin_1, R5.Pin_0

notes:
  Slide Potentiometer Pins are numbered below the potentiometer
  Pin 1 to GND
  Pin 2 to Bela Analog Input
  Pin 3 to 3.3V
  Resisors are 10k Ohm

custom parts:
  Bela: Bela low-latency audio/sensor platform
